# Fritzing sketch fritzing (saved by Fritzing 0.9.2b)
circuit board: 3.82411cm x 3.46428cm
breadboards: 1

parts:
  U1_TSOP4838 = IR Receiver Breakout [package=PCB]
  C1 = Ceramic Capacitor [capacitance=100nF package="100 mil [THT, multilayer]"]
  U1_ATtiny45 = ATTINY45 [package=dip]
  Q1 = PNP-Transistor [package="TO92 [THT]"]
  R2 = Resistor [tolerance=±5% resistance=330 package=THT]
  LED1 = LED - 5mm [color="Green (570nm)" package="5 mm [THT]"]
  LED2 = LED - 5mm [color="Red (633nm)" package="5 mm [THT]"]
  R6 = Resistor [tolerance=±5% resistance=100k package=THT]
  R7 = Resistor [tolerance=±5% resistance=100k package=THT]
  C2 = Ceramic Capacitor [capacitance=100nF voltage=6.3V package="200 mil [THT, multilayer]"]
  R4 = Trimmer Potentiometer [maximum_resistance=250kΩ package=THT]
  R1 = Resistor [tolerance=±5% resistance=100 package=THT]
  Q2 = NPN-Transistor [package="TO92 [THT]"]
  LED3 = LED - 5mm [color="Infrared (850nm)" package="5 mm [THT]"]
  R5 = Resistor [tolerance=±5% resistance=150 package=THT]
  Q3 = LTR-301 [package=ltr-301]
  R8 = Resistor [tolerance=±5% resistance=100k package=THT]

nets (from the schematic view):
  GND: U1_TSOP4838.GND, C1.0, U1_ATtiny45.GND, R2.Pin_1, C2.0, R4.leg1, LED3.cathode
  N1: U1_TSOP4838.OUT, U1_ATtiny45.PB1(MISO), Q1.B
  N2: U1_TSOP4838.VCC, C2.1, R1.Pin_0
  5V: C1.1, U1_ATtiny45.VCC, LED1.anode, R6.Pin_0, R1.Pin_1, R5.Pin_1, Q3.C
  N3: U1_ATtiny45.PB3(ADC3), R8.Pin_0
  N4: U1_ATtiny45.PB0(MOSI), Q2.B
  N5: U1_ATtiny45.PB2(SCK_ADC1), R7.Pin_0
  N6: Q1.E, LED1.cathode
  N7: Q1.C, R2.Pin_0
  N8: LED2.cathode, LED3.anode
  N9: LED2.anode, Q2.E
  N10: R6.Pin_1, R4.leg2
  N11: R7.Pin_1, R4.wiper
  N12: Q2.C, R5.Pin_0
  N13: Q3.E, R8.Pin_1
