# Fritzing sketch fritzing_TSOP4838 (saved by Fritzing 0.9.3b)
circuit board: 4.01963cm x 2.69661cm
breadboards: 1

parts:
  C1 = Ceramic Capacitor [capacitance=100nF package="100 mil [THT, multilayer]"]
  U2 = ATTINY45 [part_number=ATtiny45 package=dip]
  Q1 = PNP-Transistor [part_number=BC558B package="TO92 [THT]"]
  R2 = Resistor [tolerance=±5% resistance=330 package=THT]
  LED1 = LED - 5mm [color="Green (570nm)" package="5 mm [THT]"]
  R1 = Resistor [tolerance=±5% resistance=100 package=THT]
  Q2 = NPN-Transistor [part_number=BC548C package="TO92 [THT]"]
  R5 = Resistor [tolerance=±5% resistance=330 package=THT]
  JP1 = FTDI_BASIC [package=ftdi_basic]
  LED2 = LED - 5mm [color="Red (633nm)" package="5 mm [THT]"]
  R6 = Trimmer Potentiometer [maximum_resistance=250kΩ package=THT]
  R7 = Resistor [tolerance=±5% resistance=100k package=THT]
  R8 = Resistor [tolerance=±5% resistance=100k package=THT]
  C2 = Ceramic Capacitor [capacitance=100nF voltage=6.3V package="200 mil [THT, multilayer]"]
  U1 = IR Receiver Breakout [package=PCB]

nets (from the pcb view):
  N1: C1.0, U2.GND, R2.Pin_1, JP1.2, JP1.3, LED2.cathode, R6.leg1, C2.0, U1.OUT
  N2: C1.1, U2.VCC, LED1.anode, R1.Pin_1, R5.Pin_1, JP1.5, JP1.4, R6.leg2
  N3: U2.PB3(ADC3), R7.Pin_0
  N4: U2.PB4(ADC2), JP1.1
  N5: U2.PB0(MOSI), Q2.B
  N6: U2.PB1(MISO), JP1.6
  N7: U2.PB2(SCK_ADC1), R8.Pin_0
  N8: Q1.E, LED1.cathode
  N9: Q1.B, R8.Pin_1, U1.GND
  N10: Q1.C, R2.Pin_0
  N11: R1.Pin_0, C2.1, U1.VCC
  N12: Q2.E, LED2.anode
  N13: Q2.C, R5.Pin_0
  N14: R6.wiper, R7.Pin_1

notes:
  RasPelikan
  SilverScreenIR
